// Logisim project Logisim-104-148.circ as structural Verilog: 4 circuits, main circuit Internal Lights
module DEMUX (
  input  in_1,
  input  MSB,
  input  LSB,
  output I0,
  output I1,
  output I2,
  output I3
);

  wire not_1_out, not_2_out, not_3_out, not_4_out;

  not not_1 (not_1_out, MSB);
  not not_2 (not_2_out, LSB);
  not not_3 (not_3_out, MSB);
  not not_4 (not_4_out, LSB);
  and and_1 (I0, not_1_out, not_2_out, in_1);
  and and_2 (I1, not_3_out, LSB, in_1);
  and and_3 (I2, MSB, not_4_out, in_1);
  and and_4 (I3, MSB, LSB, in_1);

  // Notes on the sheet:
  //   1x4 DEMUX
endmodule

module MUX (
  input  I0,
  input  I1,
  input  I2,
  input  I3,
  input  MSB,
  input  LSB,
  output out_7
);

  wire and_1_out, and_2_out, and_3_out, and_4_out, not_1_out, not_2_out, not_3_out, not_4_out;

  not not_1 (not_1_out, MSB);
  not not_2 (not_2_out, LSB);
  not not_3 (not_3_out, MSB);
  not not_4 (not_4_out, LSB);
  and and_1 (and_1_out, not_1_out, not_2_out, I0);
  and and_2 (and_2_out, not_3_out, LSB, I1);
  and and_3 (and_3_out, MSB, not_4_out, I2);
  and and_4 (and_4_out, MSB, LSB, I3);
  or or_1 (out_7, and_1_out, and_2_out, and_3_out, and_4_out);

  // Notes on the sheet:
  //   4x1 MUX
endmodule

module Internal_Lights (
  input  DOOR_1,
  input  DOOR_2,
  input  DOOR_3,
  input  DOOR_4,
  input  in_5,
  input  MSB,
  input  LSB
);

  wire mux_1_out_7, or_1_out;

  or or_1 (or_1_out, DOOR_1, DOOR_2, DOOR_3, DOOR_4, in_5);
  MUX mux_1 (.I0(1'b1), .I1(or_1_out), .I2(1'b0), .I3(1'b0), .MSB(MSB), .LSB(LSB), .out_7(mux_1_out_7));
  LED led_1 (.in(mux_1_out_7));

  // Notes on the sheet:
  //   Key inserted at driver's door
  //   OFF
  //   ON
  //   CAR LIGHT CONTROLLER - INTERNAL LIGHT
  //   4x1 MUX
  //   MAIN SWITCH
  //   KEY:
  //   00 -> On
  //   10 -> OFF
  //   01 -> Door
  //   11 -> Invalid(Off)
  //   Internal Light
endmodule

module External_Lights (
  input  MSB,
  input  LSB
);

  wire and_1_out, and_2_out, clock_1_out, demux_1_i0, demux_1_i1, demux_1_i2, demux_1_i3, mux_1_out_7,
       mux_2_out_7, not_1_out, not_2_out, not_3_out, not_4_out;

  DEMUX demux_1 (.in_1(1'b1), .MSB(MSB), .LSB(LSB), .I0(demux_1_i0), .I1(demux_1_i1), .I2(demux_1_i2), .I3(demux_1_i3));
  not not_1 (not_1_out, demux_1_i0);
  not not_2 (not_2_out, demux_1_i1);
  not not_3 (not_3_out, demux_1_i0);
  not not_4 (not_4_out, demux_1_i2);
  MUX mux_1 (
    .I0(not_1_out), .I1(not_2_out), .I2(demux_1_i2), .I3(demux_1_i3), .MSB(MSB), .LSB(LSB),
    .out_7(mux_1_out_7));
  MUX mux_2 (
    .I0(not_3_out), .I1(demux_1_i1), .I2(not_4_out), .I3(demux_1_i3), .MSB(MSB), .LSB(LSB),
    .out_7(mux_2_out_7));
  Clock clock_1 (.out(clock_1_out));
  and and_1 (and_1_out, clock_1_out, mux_1_out_7);
  and and_2 (and_2_out, clock_1_out, mux_2_out_7);
  LED led_1 (.in(and_1_out));
  LED led_2 (.in(and_2_out));

  // Notes on the sheet:
  //   4x1 DEMUX
  //   4x1 MUX
  //   4x1 MUX
  //   CONTROLS
  //   Clock
  //   CAR LIGHT CONTROLLER - EXTERNAL LIGHTS
  //   KEY:
  //   00 -> Both Indicators Off
  //   01 -> Right Indicator
  //   10 -> Left Indicator
  //   11 -> Breakdown Indicator
  //   Left Indicator
  //   Right Indicator
endmodule
