// Logisim project Flip-Flops.circ as structural Verilog: 3 circuits, main circuit SR Latch
module SR_Latch (
  input  in_1,
  input  in_2,
  output out_3,
  output out_4
);

  nand nand_1 (out_3, in_1, out_4);
  nand nand_2 (out_4, out_3, in_2);
endmodule

module JK_FF (
  input  in_1,
  input  in_2,
  input  in_3,
  output out_4,
  output out_5
);

  wire clock_1_out, nand_1_out, nand_2_out;

  Clock clock_1 (.out(clock_1_out));
  nand nand_1 (nand_1_out, out_5, in_1, clock_1_out);
  nand nand_2 (nand_2_out, clock_1_out, in_3, out_4);
  nand nand_3 (out_4, nand_1_out, in_2, out_5);
  nand nand_4 (out_5, out_4, in_2, nand_2_out);
endmodule

module JK_Master_Slave (
  input  J,
  input  K,
  input  CLR_prime,
  output Q,
  output Q_prime
);

  wire clock_1_out, nand_1_out, nand_2_out, nand_3_out, nand_4_out, nand_5_out, nand_6_out, nand_7_out,
       nand_8_out, not_1_out, not_2_out;

  Clock clock_1 (.out(clock_1_out));
  not not_1 (not_1_out, clock_1_out);
  nand nand_1 (nand_1_out, Q_prime, J, not_1_out);
  nand nand_2 (nand_2_out, not_1_out, K, Q);
  nand nand_3 (nand_3_out, nand_1_out, nand_4_out);
  nand nand_4 (nand_4_out, nand_3_out, nand_2_out);
  nand nand_5 (nand_5_out, nand_3_out, clock_1_out);
  nand nand_6 (nand_6_out, clock_1_out, nand_4_out);
  nand nand_7 (nand_7_out, nand_5_out, nand_8_out);
  nand nand_8 (nand_8_out, nand_7_out, nand_6_out);
  not not_2 (not_2_out, CLR_prime);
  and and_1 (Q, nand_7_out, CLR_prime);
  or or_1 (Q_prime, nand_8_out, not_2_out);

  // Notes on the sheet:
  //   CLK
endmodule
