// Logisim project 16CO104-L4.circ as structural Verilog: 2 circuits, main circuit main
module main (
  input  LOAD,
  input  P0,
  input  P1,
  input  P2,
  input  P3,
  output Out1,
  output Out2,
  output Out3,
  output Out4
);

  wire and_1_out, and_2_out, and_3_out, and_4_out, and_5_out, and_6_out, and_7_out, and_8_out, clock_1_out,
       not_1_out, not_2_out, not_3_out, not_4_out, or_1_out, or_2_out, or_3_out, or_4_out;

  Clock clock_1 (.out(clock_1_out));
  not not_1 (not_1_out, LOAD);
  not not_2 (not_2_out, LOAD);
  not not_3 (not_3_out, LOAD);
  not not_4 (not_4_out, LOAD);
  and and_1 (and_1_out, Out1, not_1_out);
  or or_1 (or_1_out, and_1_out, and_2_out);
  and and_2 (and_2_out, P0, LOAD);
  and and_3 (and_3_out, Out2, not_2_out);
  or or_2 (or_2_out, and_3_out, and_4_out);
  and and_4 (and_4_out, P1, LOAD);
  and and_5 (and_5_out, Out3, not_3_out);
  or or_3 (or_3_out, and_5_out, and_6_out);
  and and_6 (and_6_out, P2, LOAD);
  and and_7 (and_7_out, Out4, not_4_out);
  or or_4 (or_4_out, and_7_out, and_8_out);
  and and_8 (and_8_out, P3, LOAD);
  D_Flip_Flop d_flip_flop_1 (.D(or_1_out), .CLK(clock_1_out), .out_3(Out1));
  D_Flip_Flop d_flip_flop_2 (.D(or_2_out), .CLK(clock_1_out), .out_3(Out2));
  D_Flip_Flop d_flip_flop_3 (.D(or_3_out), .CLK(clock_1_out), .out_3(Out3));
  D_Flip_Flop d_flip_flop_4 (.D(or_4_out), .CLK(clock_1_out), .out_3(Out4));

  // Notes on the sheet:
  //   CLK
  //   4 Bit Register with Parallel Load
  //   D Flip Flop
  //   D Flip Flop
  //   D Flip Flop
  //   D Flip Flop
endmodule

module D_Flip_Flop (
  input  D,
  input  CLK,
  output out_3
);

  wire nand_1_out, nand_2_out, nand_3_out, nand_4_out, nand_5_out, nand_6_out, nand_8_out, not_1_out,
       not_2_out, not_3_out;

  not not_1 (not_1_out, CLK);
  not not_2 (not_2_out, D);
  nand nand_1 (nand_1_out, D, not_1_out);
  nand nand_2 (nand_2_out, not_1_out, not_2_out);
  nand nand_3 (nand_3_out, 1'b1, nand_1_out, nand_4_out);
  nand nand_4 (nand_4_out, nand_3_out, nand_2_out, 1'b1);
  not not_3 (not_3_out, nand_3_out);
  nand nand_5 (nand_5_out, nand_3_out, CLK);
  nand nand_6 (nand_6_out, CLK, not_3_out);
  nand nand_7 (out_3, 1'b1, nand_5_out, nand_8_out);
  nand nand_8 (nand_8_out, out_3, nand_6_out, 1'b1);
endmodule
