// Logisim project 16CO104-L5.circ as structural Verilog: 2 circuits, main circuit main
module main (
  input  Serial_Input,
  output out_2,
  output out_3,
  output out_4,
  output Serial_Output
);

  wire clock_1_out;

  Clock clock_1 (.out(clock_1_out));
  D_Flip_Flop d_flip_flop_1 (.D(Serial_Input), .CLK(clock_1_out), .out_3(out_2));
  D_Flip_Flop d_flip_flop_2 (.D(out_2), .CLK(clock_1_out), .out_3(out_3));
  D_Flip_Flop d_flip_flop_3 (.D(out_3), .CLK(clock_1_out), .out_3(out_4));
  D_Flip_Flop d_flip_flop_4 (.D(out_4), .CLK(clock_1_out), .out_3(Serial_Output));

  // Notes on the sheet:
  //   CLK
  //   Serial In Serial Out (SISO) Right Shift Register
  //   D Flip Flop
endmodule

module D_Flip_Flop (
  input  D,
  input  CLK,
  output out_3
);

  wire nand_1_out, nand_2_out, nand_3_out, nand_4_out, nand_5_out, nand_6_out, nand_8_out, not_1_out,
       not_2_out, not_3_out;

  not not_1 (not_1_out, CLK);
  not not_2 (not_2_out, D);
  nand nand_1 (nand_1_out, D, not_1_out);
  nand nand_2 (nand_2_out, not_1_out, not_2_out);
  nand nand_3 (nand_3_out, 1'b1, nand_1_out, nand_4_out);
  nand nand_4 (nand_4_out, nand_3_out, nand_2_out, 1'b1);
  not not_3 (not_3_out, nand_3_out);
  nand nand_5 (nand_5_out, nand_3_out, CLK);
  nand nand_6 (nand_6_out, CLK, not_3_out);
  nand nand_7 (out_3, 1'b1, nand_5_out, nand_8_out);
  nand nand_8 (nand_8_out, out_3, nand_6_out, 1'b1);

  // Notes on the sheet:
  //   D Flip Flop
endmodule
