// Logisim project  16CO104-L1.circ as structural Verilog: 2 circuits, main circuit main
module main (
  input  in_1,
  input  in_2,
  input  in_3,
  input  in_4,
  input  in_5,
  input  in_6,
  input  in_7,
  input  in_8,
  output C4,
  output S3,
  output S2,
  output S1,
  output S0
);

  wire and_1_out, and_2_out, and_3_out, and_4_out, and_5_out, and_6_out, carry_propagate_1_out_3,
       carry_propagate_1_out_4, carry_propagate_2_out_3, carry_propagate_2_out_4, carry_propagate_3_out_3,
       carry_propagate_3_out_4, carry_propagate_4_out_4, or_1_out, or_3_out;

  Carry_propagate carry_propagate_1 (
    .in_1(in_1), .in_2(in_2), .out_3(carry_propagate_1_out_3), .out_4(carry_propagate_1_out_4));
  Carry_propagate carry_propagate_2 (
    .in_1(in_3), .in_2(in_4), .out_3(carry_propagate_2_out_3), .out_4(carry_propagate_2_out_4));
  Carry_propagate carry_propagate_3 (
    .in_1(in_5), .in_2(in_6), .out_3(carry_propagate_3_out_3), .out_4(carry_propagate_3_out_4));
  Carry_propagate carry_propagate_4 (.in_1(in_7), .in_2(in_8), .out_3(S0), .out_4(carry_propagate_4_out_4));
  and and_1 (and_1_out, carry_propagate_1_out_3, carry_propagate_2_out_4);
  and and_2 (and_2_out, carry_propagate_1_out_3, carry_propagate_2_out_3, carry_propagate_3_out_4);
  and and_3 (and_3_out, carry_propagate_2_out_3, carry_propagate_3_out_4);
  and and_4 (and_4_out, carry_propagate_2_out_3, carry_propagate_3_out_3, carry_propagate_4_out_4);
  and and_5 (and_5_out, carry_propagate_1_out_3, carry_propagate_2_out_3, carry_propagate_3_out_3, carry_propagate_4_out_4);
  or or_1 (or_1_out, carry_propagate_3_out_4, and_6_out);
  and and_6 (and_6_out, carry_propagate_3_out_3, carry_propagate_4_out_4);
  or or_2 (C4, carry_propagate_1_out_4, and_1_out, and_2_out, and_5_out);
  xor xor_1 (S3, carry_propagate_1_out_3, or_3_out);
  or or_3 (or_3_out, carry_propagate_2_out_4, and_3_out, and_4_out);
  xor xor_2 (S2, carry_propagate_2_out_3, or_1_out);
  xor xor_3 (S1, carry_propagate_3_out_3, carry_propagate_4_out_4);
endmodule

module Carry_propagate (
  input  in_1,
  input  in_2,
  output out_3,
  output out_4
);

  xor xor_1 (out_3, in_1, in_2);
  and and_1 (out_4, in_1, in_2);
endmodule
