// Logisim project 16CO104-L2.circ as structural Verilog: 2 circuits, main circuit main
module main (
  input  A3,
  input  A2,
  input  A1,
  input  A0,
  output out_5,
  output out_6,
  output out_7,
  output out_8,
  output out_9,
  output out_10,
  output out_11
);

  wire and_1_out, and_2_out, and_3_out, and_4_out, and_5_out, and_6_out, and_7_out, and_8_out, and_9_out,
       and_10_out, and_11_out, and_12_out, and_13_out, and_14_out, not_1_out, not_2_out, not_3_out,
       not_4_out, or_1_out, xor_1_out;

  not not_1 (not_1_out, A3);
  not not_2 (not_2_out, A2);
  not not_3 (not_3_out, A1);
  not not_4 (not_4_out, A0);
  and and_1 (and_1_out, not_4_out, not_3_out);
  or or_1 (or_1_out, not_3_out, not_4_out);
  and and_2 (and_2_out, not_2_out, not_4_out);
  and and_3 (and_3_out, A0, A2);
  and and_4 (and_4_out, A0, A1);
  and and_5 (and_5_out, not_4_out, not_3_out);
  and and_6 (and_6_out, not_2_out, not_1_out);
  and and_7 (and_7_out, not_4_out, A1);
  and and_8 (and_8_out, A1, not_2_out);
  and and_9 (and_9_out, not_2_out, not_4_out);
  and and_10 (and_10_out, not_3_out, A0, A2);
  and and_11 (and_11_out, not_4_out, not_2_out);
  and and_12 (and_12_out, A1, not_4_out);
  xor xor_1 (xor_1_out, A1, A2);
  and and_13 (and_13_out, A1, not_4_out);
  and and_14 (and_14_out, or_1_out, A2);
  or or_2 (out_5, and_1_out, and_14_out, A3);
  or or_3 (out_6, and_2_out, and_3_out, A3, A1);
  or or_4 (out_7, and_4_out, and_5_out, and_6_out, A3);
  or or_5 (out_8, A3, A2, not_3_out, A0);
  or or_6 (out_9, and_7_out, and_8_out, and_9_out, and_10_out, A3);
  or or_7 (out_10, and_11_out, and_12_out);
  or or_8 (out_11, xor_1_out, and_13_out, A3);
endmodule

module _7_segment (
  input  in_1,
  input  in_2,
  input  in_3,
  input  in_4,
  output out_5,
  output out_6,
  output out_7,
  output out_8,
  output out_9,
  output out_10,
  output out_11
);

  main main_1 (
    .A3(in_1), .A2(in_2), .A1(in_3), .A0(in_4), .out_5(out_6), .out_6(out_5), .out_7(out_7), .out_8(out_10),
    .out_9(out_11), .out_10(out_9), .out_11(out_8));
endmodule
